# Fritzing sketch Untitled Sketch 2 (saved by Fritzing 0.9.3b)
breadboards: 1

parts:
  Part1 = Arduino Uno (Rev3)
  S2 = Pushbutton [package="[THT]"]
  R1 = Resistor [tolerance=±5% resistance=220 package=THT]
  S3 = Pushbutton [package="[THT]"]
  S4 = Pushbutton [package="[THT]"]
  S5 = Pushbutton [package="[THT]"]
  R2 = Resistor [tolerance=±5% resistance=220 package=THT]
  R3 = Resistor [tolerance=±5% resistance=220 package=THT]
  R4 = Resistor [tolerance=±5% resistance=220 package=THT]
  S6 = Pushbutton [package="[THT]"]
  R5 = Resistor [tolerance=±5% resistance=220 package=THT]
  Relay_5V1 = Keyes Relay [package=THT]

nets:
  N1: Part1.D8, Relay_5V1.signal
  N2: Part1.D3_PWM, R1.Pin_0, S4.Pin_3, S4.Pin_4
  N3: Part1.D4, S3.Pin_3, S3.Pin_4, R2.Pin_0
  N4: Part1.D5_PWM, S2.Pin_3, S2.Pin_4, R3.Pin_0
  N5: Part1.D6_PWM, S5.Pin_3, S5.Pin_4, R4.Pin_0
  N6: Part1.D7, S6.Pin_3, S6.Pin_4, R5.Pin_0
  N7: Part1.5V, R1.Pin_1, R2.Pin_1, R3.Pin_1, R4.Pin_1, R5.Pin_1, Relay_5V1.power
  N8: Part1.GND, S2.Pin_1, S2.Pin_2, S3.Pin_1, S3.Pin_2, S4.Pin_1, S4.Pin_2, S5.Pin_1, S5.Pin_2, S6.Pin_1, S6.Pin_2, Relay_5V1.ground

custom parts:
  Keyes Relay: The Keyes 5V relay module is suitable for SCM development, home appliance control. It uses a 5V~12V TIL control signal which can control DC / AC signal.
